// Digital circuit piscapiscaFLIPFLOP.dig as structural Verilog
module piscapiscaFLIPFLOP (
  input  HAZ,
  input  LEFT,
  input  RIGHT,
  input  C
);

  wire and_1_out, and_2_out, and_3_out, and_4_out, and_5_out, and_6_out, and_7_out, and_8_out, and_9_out,
       and_10_out, and_11_out, and_12_out, and_13_out, and_14_out, and_15_out, and_16_out, and_17_out,
       and_18_out, and_19_out, and_20_out, and_21_out, and_22_out, and_23_out, and_24_out, and_25_out,
       and_26_out, and_27_out, and_28_out, and_29_out, and_30_out, and_31_out, and_32_out, and_33_out,
       and_34_out, and_35_out, and_36_out, and_37_out, and_38_out, and_39_out, and_40_out, and_41_out,
       and_42_out, and_43_out, and_44_out, and_45_out, and_46_out, and_47_out, and_48_out, and_49_out,
       and_50_out, and_51_out, and_52_out, and_53_out, and_54_out, and_55_out, and_56_out, and_57_out,
       and_58_out, and_59_out, and_60_out, and_61_out, and_62_out, and_63_out, and_64_out, and_65_out,
       and_66_out, and_67_out, and_68_out, and_69_out, and_70_out, and_71_out, and_72_out, and_73_out,
       and_74_out, and_75_out, and_76_out, and_77_out, and_78_out, and_79_out, and_80_out, not_1_out,
       not_2_out, not_3_out, not_4_out, not_5_out, not_6_out, not_7_out, not_8_out, or_1_out, or_2_out,
       or_3_out, or_4_out, or_5_out, or_6_out, Q_0_n, Q_1_n, Q_2_n, Q_3_n, Q_4_n, Q_5_n;

  not not_1 (not_1_out, LEFT);
  not not_2 (not_2_out, RIGHT);
  not not_3 (not_3_out, Q_5_n);
  not not_4 (not_4_out, Q_4_n);
  not not_5 (not_5_out, Q_3_n);
  not not_6 (not_6_out, Q_2_n);
  not not_7 (not_7_out, Q_1_n);
  not not_8 (not_8_out, Q_0_n);
  and and_1 (and_1_out, HAZ, not_8_out, not_2_out);
  and and_2 (and_2_out, HAZ, not_1_out, not_8_out);
  and and_3 (and_3_out, HAZ, not_7_out, not_2_out);
  and and_4 (and_4_out, HAZ, not_1_out, not_7_out);
  and and_5 (and_5_out, HAZ, not_6_out, not_2_out);
  and and_6 (and_6_out, HAZ, not_1_out, not_6_out);
  and and_7 (and_7_out, HAZ, not_5_out, not_2_out);
  and and_8 (and_8_out, HAZ, not_1_out, not_5_out);
  and and_9 (and_9_out, HAZ, not_4_out, not_2_out);
  and and_10 (and_10_out, HAZ, not_1_out, not_4_out);
  and and_11 (and_11_out, HAZ, not_3_out, not_2_out);
  and and_12 (and_12_out, HAZ, not_1_out, not_3_out);
  and and_13 (and_13_out, LEFT, not_8_out, not_7_out, not_6_out, Q_3_n, Q_4_n, not_3_out, not_2_out);
  and and_14 (and_14_out, HAZ, not_8_out, not_2_out);
  and and_15 (and_15_out, HAZ, not_1_out, not_8_out);
  and and_16 (and_16_out, HAZ, not_7_out, not_2_out);
  and and_17 (and_17_out, HAZ, not_1_out, not_7_out);
  and and_18 (and_18_out, HAZ, not_6_out, not_2_out);
  and and_19 (and_19_out, HAZ, not_1_out, not_6_out);
  and and_20 (and_20_out, HAZ, not_5_out, not_2_out);
  and and_21 (and_21_out, HAZ, not_1_out, not_5_out);
  and and_22 (and_22_out, HAZ, not_4_out, not_2_out);
  and and_23 (and_23_out, HAZ, not_1_out, not_4_out);
  and and_24 (and_24_out, HAZ, not_3_out, not_2_out);
  and and_25 (and_25_out, HAZ, not_1_out, not_3_out);
  and and_26 (and_26_out, LEFT, not_8_out, not_7_out, not_6_out, Q_3_n, not_3_out, not_2_out);
  and and_27 (and_27_out, HAZ, not_8_out, not_2_out);
  and and_28 (and_28_out, HAZ, not_1_out, not_8_out);
  and and_29 (and_29_out, HAZ, not_7_out, not_2_out);
  and and_30 (and_30_out, HAZ, not_1_out, not_7_out);
  and and_31 (and_31_out, HAZ, not_6_out, not_2_out);
  and and_32 (and_32_out, HAZ, not_1_out, not_6_out);
  and and_33 (and_33_out, HAZ, not_5_out, not_2_out);
  and and_34 (and_34_out, HAZ, not_1_out, not_5_out);
  and and_35 (and_35_out, HAZ, not_4_out, not_2_out);
  and and_36 (and_36_out, HAZ, not_1_out, not_4_out);
  and and_37 (and_37_out, HAZ, not_3_out, not_2_out);
  and and_38 (and_38_out, HAZ, not_1_out, not_3_out);
  and and_39 (and_39_out, LEFT, not_8_out, not_7_out, not_6_out, Q_3_n, not_3_out, not_2_out);
  and and_40 (and_40_out, LEFT, not_8_out, not_7_out, not_6_out, not_4_out, not_3_out, not_2_out);
  and and_41 (and_41_out, HAZ, not_8_out, not_2_out);
  and and_42 (and_42_out, HAZ, not_1_out, not_8_out);
  and and_43 (and_43_out, HAZ, not_7_out, not_2_out);
  and and_44 (and_44_out, HAZ, not_1_out, not_7_out);
  and and_45 (and_45_out, HAZ, not_6_out, not_2_out);
  and and_46 (and_46_out, HAZ, not_1_out, not_6_out);
  and and_47 (and_47_out, HAZ, not_5_out, not_2_out);
  and and_48 (and_48_out, HAZ, not_1_out, not_5_out);
  and and_49 (and_49_out, HAZ, not_4_out, not_2_out);
  and and_50 (and_50_out, HAZ, not_1_out, not_4_out);
  and and_51 (and_51_out, HAZ, not_3_out, not_2_out);
  and and_52 (and_52_out, HAZ, not_1_out, not_3_out);
  and and_53 (and_53_out, not_1_out, not_8_out, not_7_out, not_5_out, not_4_out, not_3_out, RIGHT);
  and and_54 (and_54_out, not_1_out, not_8_out, Q_2_n, not_5_out, not_4_out, not_3_out, RIGHT);
  and and_55 (and_55_out, HAZ, not_8_out, not_2_out);
  and and_56 (and_56_out, HAZ, not_1_out, not_8_out);
  and and_57 (and_57_out, HAZ, not_7_out, not_2_out);
  and and_58 (and_58_out, HAZ, not_1_out, not_7_out);
  and and_59 (and_59_out, HAZ, not_6_out, not_2_out);
  and and_60 (and_60_out, HAZ, not_1_out, not_6_out);
  and and_61 (and_61_out, HAZ, not_5_out, not_2_out);
  and and_62 (and_62_out, HAZ, not_1_out, not_5_out);
  and and_63 (and_63_out, HAZ, not_4_out, not_2_out);
  and and_64 (and_64_out, HAZ, not_1_out, not_4_out);
  and and_65 (and_65_out, HAZ, not_3_out, not_2_out);
  and and_66 (and_66_out, HAZ, not_1_out, not_3_out);
  and and_67 (and_67_out, not_1_out, not_8_out, Q_2_n, not_5_out, not_4_out, not_3_out, RIGHT);
  and and_68 (and_68_out, HAZ, not_8_out, not_2_out);
  and and_69 (and_69_out, HAZ, not_1_out, not_8_out);
  and and_70 (and_70_out, HAZ, not_7_out, not_2_out);
  and and_71 (and_71_out, HAZ, not_1_out, not_7_out);
  and and_72 (and_72_out, HAZ, not_6_out, not_2_out);
  and and_73 (and_73_out, HAZ, not_1_out, not_6_out);
  and and_74 (and_74_out, HAZ, not_5_out, not_2_out);
  and and_75 (and_75_out, HAZ, not_1_out, not_5_out);
  and and_76 (and_76_out, HAZ, not_4_out, not_2_out);
  and and_77 (and_77_out, HAZ, not_1_out, not_4_out);
  and and_78 (and_78_out, HAZ, not_3_out, not_2_out);
  and and_79 (and_79_out, HAZ, not_1_out, not_3_out);
  and and_80 (and_80_out, not_1_out, not_8_out, Q_1_n, Q_2_n, not_5_out, not_4_out, not_3_out, RIGHT);
  or or_1 (or_1_out, and_1_out, and_2_out, and_3_out, and_4_out, and_5_out, and_6_out, and_7_out, and_8_out, and_9_out, and_10_out, and_11_out, and_12_out, and_13_out);
  or or_2 (or_2_out, and_14_out, and_15_out, and_16_out, and_17_out, and_18_out, and_19_out, and_20_out, and_21_out, and_22_out, and_23_out, and_24_out, and_25_out, and_26_out);
  or or_3 (or_3_out, and_55_out, and_56_out, and_57_out, and_58_out, and_59_out, and_60_out, and_61_out, and_62_out, and_63_out, and_64_out, and_65_out, and_66_out, and_67_out);
  or or_4 (or_4_out, and_68_out, and_69_out, and_70_out, and_71_out, and_72_out, and_73_out, and_74_out, and_75_out, and_76_out, and_77_out, and_78_out, and_79_out, and_80_out);
  or or_5 (or_5_out, and_27_out, and_28_out, and_29_out, and_30_out, and_31_out, and_32_out, and_33_out, and_34_out, and_35_out, and_36_out, and_37_out, and_38_out, and_39_out, and_40_out);
  or or_6 (or_6_out, and_41_out, and_42_out, and_43_out, and_44_out, and_45_out, and_46_out, and_47_out, and_48_out, and_49_out, and_50_out, and_51_out, and_52_out, and_53_out, and_54_out);
  D_FF u_Q_5_n (.D(or_1_out), .C(C), .Q(Q_5_n));  // open: nQ
  D_FF u_Q_4_n (.D(or_2_out), .C(C), .Q(Q_4_n));  // open: nQ
  D_FF u_Q_3_n (.D(or_5_out), .C(C), .Q(Q_3_n));  // open: nQ
  D_FF u_Q_2_n (.D(or_6_out), .C(C), .Q(Q_2_n));  // open: nQ
  D_FF u_Q_1_n (.D(or_3_out), .C(C), .Q(Q_1_n));  // open: nQ
  D_FF u_Q_0_n (.D(or_4_out), .C(C), .Q(Q_0_n));  // open: nQ
  LED led_1 (.in(Q_5_n));
  LED led_2 (.in(Q_4_n));
  LED led_3 (.in(Q_3_n));
  LED led_4 (.in(Q_2_n));
  LED led_5 (.in(Q_1_n));
  LED led_6 (.in(Q_0_n));
endmodule
