// Digital circuit piscapiscaROM.dig as structural Verilog
module piscapiscaROM (
  input  HAZ,
  input  LEFT,
  input  RIGHT,
  input  clk
);

  wire [5:0] d_ff_4_q, rom_1_d;

  ROM #(.AddrBits(9), .Bits(6)) rom_1 (.A({HAZ, LEFT, RIGHT, d_ff_4_q}), .sel(1'b1), .D(rom_1_d));
  D_FF d_ff_1 (.D(rom_1_d[5]), .C(clk), .Q(d_ff_4_q[5]));  // open: nQ
  D_FF d_ff_2 (.D(rom_1_d[4]), .C(clk), .Q(d_ff_4_q[4]));  // open: nQ
  D_FF d_ff_3 (.D(rom_1_d[3]), .C(clk), .Q(d_ff_4_q[3]));  // open: nQ
  D_FF d_ff_4 (.D(rom_1_d[2]), .C(clk), .Q(d_ff_4_q[2]));  // open: nQ
  D_FF d_ff_5 (.D(rom_1_d[1]), .C(clk), .Q(d_ff_4_q[1]));  // open: nQ
  D_FF d_ff_6 (.D(rom_1_d[0]), .C(clk), .Q(d_ff_4_q[0]));  // open: nQ
  LED LC (.in(d_ff_4_q[5]));
  LED LB (.in(d_ff_4_q[4]));
  LED LA (.in(d_ff_4_q[3]));
  LED RA (.in(d_ff_4_q[2]));
  LED RB (.in(d_ff_4_q[1]));
  LED RC (.in(d_ff_4_q[0]));

  // Notes on the sheet:
  //   clk: Hz: 2
  //   contents of rom_1 (hex, n*v repeats v):
  //   0,0,0,0,0,0,0,0,0,0,0,0,0,0,0,0,0,0,0,0,0,0,0,0,0,0,0,0,0,0,0,0,0,0,0,0,0,0,0,0,0,
  //   0,0,0,0,0,0,0,0,0,0,0,0,0,0,0,0,0,0,0,0,0,0,0,44,0,0,0,46,0,47,40,0,0,0,0,0,0,0,0,
  //   0,0,0,0,0,0,0,0,0,0,0,0,0,0,0,0,0,0,0,0,0,0,0,0,0,0,0,0,0,0,0,0,0,0,0,0,0,0,0,0,0,
  //   0,0,0,0,0,0,0,88,0,0,0,0,0,0,0,98,0,0,0,0,0,0,0,0,0,0,0,0,0,0,0,b8,0,0,0,0,0,0,0,
  //   0,0,0,0,0,0,0,0,0,0,0,0,0,0,0,0,0,0,0,0,0,0,0,0,80,0,0,0,0,0,0,0,0,0,0,0,0,0,0,0,
  //   0,0,0,0,0,0,0,0,0,0,0,0,0,0,0,0,0,0,0,0,0,0,0,0,0,0,0,0,0,0,0,0,0,0,0,0,0,0,0,0,0,
  //   0,0,0,0,0,0,0,0,0,0,0,0,0,0,0,1ff,1ff,1ff,1ff,1ff,1ff,1ff,1ff,1ff,1ff,1ff,1ff,1ff,
  //   1ff,1ff,1ff,1ff,1ff,1ff,1ff,1ff,1ff,1ff,1ff,1ff,1ff,1ff,1ff,1ff,1ff,1ff,1ff,1ff,1ff,
  //   1ff,1ff,1ff,1ff,1ff,1ff,1ff,1ff,1ff,1ff,1ff,1ff,1ff,1ff,1ff,1ff,1ff,1ff,1ff,1ff,1ff,
  //   1ff,1ff,1ff,1ff,1ff,1ff,1ff,1ff,0,1ff,1ff,1ff,1ff,1ff,1ff,1ff,1ff,1ff,1ff,1ff,1ff,
  //   1ff,1ff,1ff,1ff,1ff,1ff,1ff,1ff,1ff,1ff,1ff,1ff,1ff,1ff,1ff,1ff,1ff,1ff,1ff,1ff,1ff,
  //   1ff,1ff,1ff,1ff,1ff,1ff,1ff,1ff,1ff,1ff,1ff,1ff,1ff,1ff,1ff,1ff,1ff,1ff,1ff,1ff,1ff,
  //   1ff,1ff,1ff,1ff,1ff,1ff,1ff,1ff,1ff,0,1ff,1ff,1ff,1ff,1ff,1ff,1ff,1ff,1ff,1ff,1ff,
  //   1ff,1ff,1ff,1ff,1ff,1ff,1ff,1ff,1ff,1ff,1ff,1ff,1ff,1ff,1ff,1ff,1ff,1ff,1ff,1ff,1ff,
  //   1ff,1ff,1ff,1ff,1ff,1ff,1ff,1ff,1ff,1ff,1ff,1ff,1ff,1ff,1ff,1ff,1ff,1ff,1ff,1ff,1ff,
  //   1ff,1ff,1ff,1ff,1ff,1ff,1ff,1ff,1ff,1ff
endmodule
